// Logisim project 1.circ as structural Verilog: 4 circuits, main circuit main
module main (
  input  A,
  input  B,
  input  C,
  output D
);

  wire transistor_1_out, transistor_2_out, transistor_4_out, transistor_7_out, transistor_12_out,
       transistor_15_out, undriven, undriven_2, undriven_3, undriven_4;

  Transistor #(.\type ("n")) transistor_1 (.in(1'b0), .out(transistor_1_out), .gate(undriven_2));
  Transistor transistor_2 (.in(1'b1), .out(transistor_2_out), .gate(undriven));
  Transistor transistor_3 (.in(transistor_2_out), .out(transistor_1_out), .gate(undriven_2));
  Transistor transistor_4 (.in(1'b1), .out(transistor_4_out), .gate(A));
  Transistor #(.\type ("n")) transistor_5 (.in(1'b0), .out(transistor_1_out), .gate(undriven));
  Transistor transistor_6 (.in(transistor_4_out), .out(D), .gate(A));
  Transistor #(.\type ("n")) transistor_7 (.in(1'b0), .out(transistor_7_out), .gate(C));
  Transistor transistor_8 (.in(1'b1), .out(transistor_4_out), .gate(B));
  Transistor #(.\type ("n")) transistor_9 (.in(transistor_7_out), .out(D), .gate(A));
  Transistor transistor_10 (.in(1'b1), .out(D), .gate(C));
  Transistor #(.\type ("n")) transistor_11 (.in(1'b0), .out(transistor_7_out), .gate(B));
  Transistor transistor_12 (.in(1'b1), .out(transistor_12_out), .gate(undriven_3));
  Transistor transistor_13 (.in(1'b1), .out(transistor_12_out), .gate(undriven_4));
  Transistor #(.\type ("n")) transistor_14 (.in(transistor_15_out), .out(transistor_12_out), .gate(undriven_3));
  Transistor #(.\type ("n")) transistor_15 (.in(1'b0), .out(transistor_15_out), .gate(undriven_4));

  // Notes on the sheet:
  //   NOR
  //   NAND
endmodule

module _1 (
  input  A,
  input  B,
  output out_3,
  output out_4
);

  wire transistor_1_out, transistor_3_out, transistor_5_out, transistor_6_out, transistor_9_out,
       transistor_12_out, transistor_13_out, transistor_15_out, transistor_17_out, transistor_18_out,
       undriven;

  Transistor transistor_1 (.in(1'b1), .out(transistor_1_out), .gate(A));
  Transistor #(.\type ("n")) transistor_2 (.in(1'b0), .out(transistor_1_out), .gate(A));
  Transistor transistor_3 (.in(1'b1), .out(transistor_3_out), .gate(B));
  Transistor #(.\type ("n")) transistor_4 (.in(1'b0), .out(transistor_3_out), .gate(B));
  Transistor transistor_5 (.in(1'b1), .out(transistor_5_out), .gate(A));
  Transistor transistor_6 (.in(1'b1), .out(transistor_6_out), .gate(transistor_1_out));
  Transistor transistor_7 (.in(1'b1), .out(transistor_5_out), .gate(transistor_3_out));
  Transistor #(.\type ("n")) transistor_8 (.in(transistor_9_out), .out(transistor_5_out), .gate(A));
  Transistor #(.\type ("n")) transistor_9 (.in(1'b0), .out(transistor_9_out), .gate(transistor_3_out));
  Transistor transistor_10 (.in(1'b1), .out(transistor_6_out), .gate(B));
  Transistor #(.\type ("n")) transistor_11 (.in(transistor_12_out), .out(transistor_6_out), .gate(transistor_1_out));
  Transistor #(.\type ("n")) transistor_12 (.in(1'b0), .out(transistor_12_out), .gate(B));
  Transistor transistor_13 (.in(1'b1), .out(transistor_13_out), .gate(transistor_5_out));
  Transistor #(.\type ("n")) transistor_14 (.in(1'b0), .out(transistor_13_out), .gate(transistor_5_out));
  Transistor transistor_15 (.in(1'b1), .out(transistor_15_out), .gate(transistor_6_out));
  Transistor #(.\type ("n")) transistor_16 (.in(1'b0), .out(transistor_15_out), .gate(transistor_6_out));
  Transistor #(.\type ("n")) transistor_17 (.in(1'b0), .out(transistor_17_out), .gate(transistor_15_out));
  Transistor transistor_18 (.in(1'b1), .out(transistor_18_out), .gate(transistor_13_out));
  Transistor transistor_19 (.in(transistor_18_out), .out(transistor_17_out), .gate(transistor_15_out));
  Transistor transistor_20 (.in(1'b1), .out(out_4), .gate(transistor_17_out));
  Transistor #(.\type ("n")) transistor_21 (.in(1'b0), .out(out_4), .gate(transistor_17_out));
  Transistor #(.\type ("n")) transistor_22 (.in(1'b0), .out(transistor_17_out), .gate(transistor_13_out));
  Transistor transistor_23 (.in(1'b1), .out(out_3), .gate(undriven));
  Transistor #(.\type ("n")) transistor_24 (.in(1'b0), .out(out_3), .gate(undriven));
endmodule

module _2 (
  input  A,
  input  B,
  output G,
  output E,
  output F
);

  wire and_2_out, and_3_out, not_1_out, not_2_out, not_3_out, not_4_out;

  not not_1 (not_1_out, B);
  not not_2 (not_2_out, A);
  not not_3 (not_3_out, B);
  not not_4 (not_4_out, A);
  and and_1 (G, A, not_1_out);
  and and_2 (and_2_out, not_2_out, not_3_out);
  and and_3 (and_3_out, A, B);
  and and_4 (F, not_4_out, B);
  or or_1 (E, and_2_out, and_3_out);
endmodule

module _3 (
  input  A,
  input  C,
  input  B,
  input  D,
  output Z
);

  wire and_1_out, and_2_out, not_1_out, not_2_out, not_3_out;

  not not_1 (not_1_out, C);
  not not_2 (not_2_out, D);
  not not_3 (not_3_out, B);
  and and_1 (and_1_out, A, not_1_out, B, not_2_out);
  and and_2 (and_2_out, A, C, not_3_out, D);
  or or_1 (Z, and_1_out, and_2_out);
endmodule
